# Fritzing sketch All (saved by Fritzing 0.9.9b)
breadboards: 1

parts:
  U1 = ESP32-38PinWide [part_number=ESP32-38PinWide]
  R8 = TRIMPOT [package=3386u]
  R9 = TRIMPOT [package=3386u]
  R10 = TRIMPOT [package=3386u]
  R11 = TRIMPOT [package=3386u]
  R12 = TRIMPOT [package=3386u]
  R13 = TRIMPOT [package=3386u]
  R14 = TRIMPOT [package=3386u]
  R15 = TRIMPOT [package=3386u]
  R16 = TRIMPOT [package=3386u]
  U2 = ENCODER-QUADRATURE [package=encoder-16mm-quad]
  U3 = ENCODER-QUADRATURE [package=encoder-16mm-quad]
  U4 = ENCODER-QUADRATURE [package=encoder-16mm-quad]
  U5 = ENCODER-QUADRATURE [package=encoder-16mm-quad]
  U6 = ENCODER-QUADRATURE [package=encoder-16mm-quad]
  J1 = Basic Servo
  J3 = Basic Servo
  J4 = Basic Servo
  J5 = Basic Servo
  IC1 = SELECTOR_MULTIPLEXER [package=dil16]
  IC2 = SELECTOR_MULTIPLEXER [package=dil16]
  BAT1 = Battery Holders [package=lipo-1100mAh]
  J2 = Basic Servo

nets:
  N1: U1.3.3, IC1.A_2Y, IC1.P_GND, IC1.P_VCC, IC2.P_VCC
  N2: U1.GPIO35, IC2.A_1B
  N3: U1.GPIO32, IC1.A_2B, IC2.A_2B
  N4: U1.GPIO33, IC1.A_3Y, IC2.A_3Y
  N5: U1.GPIO25, IC1.A_3B, IC2.A_3B
  N6: U1.GPIO26, IC1.A_3A, IC2.A_3A
  N7: U1.GPIO27, IC1.A_1B
  GND: U1.GPIO11, J1.gnd, J3.gnd, J4.gnd, J5.gnd, IC2.A_2Y, IC2.P_GND, BAT1.-, J2.gnd
  N8: U1.GPIO15, J3.pulse
  N9: U1.GPIO2, J4.pulse
  N10: U1.GPIO4, J5.pulse
  N11: U1.GPIO21, J2.pulse
  N12: U1.GPIO23, J1.pulse
  N13: R8.Plus, R9.Plus
  N14: R8.Data, IC1.A_1A
  GND_2: R8.GND, R9.GND
  N15: R9.Data, IC2.A_G
  N16: R10.Data, IC1.A_2A
  N17: R11.Plus, R12.Plus
  N18: R11.Data, IC2.A_4Y
  GND_3: R11.GND, R12.GND
  N19: R12.Data, IC1.A_1Y
  N20: R13.Plus, R14.Plus
  N21: R13.Data, IC2.A_!A!_B
  GND_4: R13.GND, R14.GND
  N22: R14.Data, IC2.A_4B
  N23: R15.Plus, R16.Plus
  N24: R15.Data, IC2.A_2A
  GND_5: R15.GND, R16.GND
  N25: R16.Data, IC2.A_4A
  N26: U2.B, IC1.A_4B
  N27: U3.B, IC1.A_4A
  N28: U4.B, IC1.A_G
  N29: U5.B, IC1.A_4Y
  N30: U6.B, IC1.A_!A!_B
  VCC: J1.vcc, J3.vcc, J4.vcc, J5.vcc, BAT1.+, J2.vcc

custom parts:
  ESP32-38PinWide: Generic 38-Pin ESP32 with wide format (only access to one side of pins on a breadboard) based on Stephen Lilley's HiLetgo ESP-WROOM-32 ESP32 ESP-32S Development Board.
  TRIMPOT: Various small potentiometers for set-and-forget applications
