# Fritzing sketch OnlyData (saved by Fritzing 0.9.9b)
breadboards: 1

parts:
  U1 = ESP32-38PinWide [part_number=ESP32-38PinWide]
  R8 = TRIMPOT [package=3386u]
  R9 = TRIMPOT [package=3386u]
  R10 = TRIMPOT [package=3386u]
  R11 = TRIMPOT [package=3386u]
  R12 = TRIMPOT [package=3386u]
  R13 = TRIMPOT [package=3386u]
  R14 = TRIMPOT [package=3386u]
  R15 = TRIMPOT [package=3386u]
  R16 = TRIMPOT [package=3386u]
  U2 = ENCODER-QUADRATURE [package=encoder-16mm-quad]
  U3 = ENCODER-QUADRATURE [package=encoder-16mm-quad]
  U4 = ENCODER-QUADRATURE [package=encoder-16mm-quad]
  U5 = ENCODER-QUADRATURE [package=encoder-16mm-quad]
  U6 = ENCODER-QUADRATURE [package=encoder-16mm-quad]
  J3 = Basic Servo
  J4 = Basic Servo
  J5 = Basic Servo
  IC1 = SELECTOR_MULTIPLEXER [package=dil16]
  IC2 = SELECTOR_MULTIPLEXER [package=dil16]
  J2 = Basic Servo
  J1 = Basic Servo
  R17 = TRIMPOT [package=3386u]

nets:
  N1: U1.GPIO35, IC2.A_1B
  N2: U1.GPIO32, IC1.A_2B, IC2.A_2B
  N3: U1.GPIO33, IC1.A_3Y, IC2.A_3Y
  N4: U1.GPIO25, IC1.A_3B, IC2.A_3B
  N5: U1.GPIO26, IC1.A_3A, IC2.A_3A
  N6: U1.GPIO27, IC1.A_1B
  N7: U1.GPIO15, J3.pulse
  N8: U1.GPIO2, J4.pulse
  N9: U1.GPIO4, J5.pulse
  N10: U1.GPIO21, J2.pulse
  N11: U1.GPIO23, J1.pulse
  N12: R8.Data, IC1.A_1A
  N13: R9.Data, IC2.A_G
  N14: R10.Data, IC1.A_2A
  N15: R11.Data, IC2.A_4Y
  N16: R12.Data, IC1.A_1Y
  N17: R13.Data, IC2.A_!A!_B
  N18: R14.Data, IC2.A_4B
  N19: R15.Data, IC2.A_2A
  N20: R16.Data, IC2.A_4A
  N21: U2.B, IC1.A_4B
  N22: U3.B, IC1.A_4A
  N23: U4.B, IC1.A_G
  N24: U5.B, IC1.A_4Y
  N25: U6.B, IC1.A_!A!_B
  N26: IC2.A_1Y, R17.Data

custom parts:
  ESP32-38PinWide: Generic 38-Pin ESP32 with wide format (only access to one side of pins on a breadboard) based on Stephen Lilley's HiLetgo ESP-WROOM-32 ESP32 ESP-32S Development Board.
  TRIMPOT: Various small potentiometers for set-and-forget applications
