# Fritzing sketch OnlyElectricity (saved by Fritzing 0.9.9b)
breadboards: 1

parts:
  U1 = ESP32-38PinWide [part_number=ESP32-38PinWide]
  R8 = TRIMPOT [package=3386u]
  R9 = TRIMPOT [package=3386u]
  R10 = TRIMPOT [package=3386u]
  R11 = TRIMPOT [package=3386u]
  R12 = TRIMPOT [package=3386u]
  R13 = TRIMPOT [package=3386u]
  R14 = TRIMPOT [package=3386u]
  R15 = TRIMPOT [package=3386u]
  R16 = TRIMPOT [package=3386u]
  U2 = ENCODER-QUADRATURE [package=encoder-16mm-quad]  # not connected
  U3 = ENCODER-QUADRATURE [package=encoder-16mm-quad]  # not connected
  U4 = ENCODER-QUADRATURE [package=encoder-16mm-quad]  # not connected
  U5 = ENCODER-QUADRATURE [package=encoder-16mm-quad]  # not connected
  U6 = ENCODER-QUADRATURE [package=encoder-16mm-quad]  # not connected
  J1 = Basic Servo
  J3 = Basic Servo
  J4 = Basic Servo
  J5 = Basic Servo
  IC1 = SELECTOR_MULTIPLEXER [package=dil16]
  IC2 = SELECTOR_MULTIPLEXER [package=dil16]
  BAT1 = Battery Holders [package=lipo-1100mAh]
  J2 = Basic Servo
  R17 = TRIMPOT [package=3386u]

nets:
  N1: U1.3.3, IC1.P_VCC, IC2.P_VCC
  GND: U1.GPIO11, J1.gnd, J3.gnd, J4.gnd, J5.gnd, IC1.A_2Y, IC1.P_GND, IC2.A_2Y, IC2.P_GND, BAT1.-, J2.gnd
  N2: R8.Plus, R9.Plus
  GND_2: R8.GND, R9.GND
  N3: R10.Plus, R17.Plus
  GND_3: R10.GND, R17.GND
  N4: R11.Plus, R12.Plus
  GND_4: R11.GND, R12.GND
  N5: R13.Plus, R14.Plus
  GND_5: R13.GND, R14.GND
  N6: R15.Plus, R16.Plus
  GND_6: R15.GND, R16.GND
  VCC: J1.vcc, J3.vcc, J4.vcc, J5.vcc, BAT1.+, J2.vcc

custom parts:
  ESP32-38PinWide: Generic 38-Pin ESP32 with wide format (only access to one side of pins on a breadboard) based on Stephen Lilley's HiLetgo ESP-WROOM-32 ESP32 ESP-32S Development Board.
  TRIMPOT: Various small potentiometers for set-and-forget applications
